// Logisim project F2_design.circ as structural Verilog: 1 circuit, main circuit main
module main (
);

  wire and_1_out, and_2_out, and_3_out, and_4_out, dipswitch_1_sw1, dipswitch_1_sw2, not_1_out, not_2_out;

  DipSwitch dipswitch_1 (.sw1(dipswitch_1_sw1), .sw2(dipswitch_1_sw2));  // open: sw3, sw4, sw5, sw6, sw7, sw8
  not not_1 (not_1_out, dipswitch_1_sw1);
  not not_2 (not_2_out, dipswitch_1_sw2);
  and and_1 (and_1_out, not_1_out, not_2_out);
  and and_2 (and_2_out, dipswitch_1_sw2, not_1_out);
  and and_3 (and_3_out, dipswitch_1_sw1, not_2_out);
  and and_4 (and_4_out, dipswitch_1_sw2, dipswitch_1_sw1);
  LED L00 (.in(and_1_out));
  LED L01 (.in(and_2_out));
  LED L10 (.in(and_3_out));
  LED L11 (.in(and_4_out));

  // Notes on the sheet:
  //   2-4译码器
endmodule
