// Logisim project F2_tutorial.circ as structural Verilog: 2 circuits, main circuit main
module main (
  input  inputalabel,
  input  inputb,
  output output1
);

  wire and1_out, and_1_out, not_1_out, not_2_out;

  XOR1 xor1_1 ();  // open: inputalabel, inputb, in_3, in_4, in_5, output1, out_7
  not not_1 (not_1_out, inputb);
  not not_2 (not_2_out, inputalabel);
  and and1 (and1_out, inputalabel, not_1_out);
  and and_1 (and_1_out, not_2_out, inputb);
  or or_1 (output1, and1_out, and_1_out);

  // Notes on the sheet:
  //   XOR
endmodule

module XOR1 (
  input  inputalabel,
  input  inputb,
  input  in_3,
  input  in_4,
  input  in_5,
  output output1,
  output out_7
);

  wire and_1_out, and_2_out, and_3_out, d_ff_1_qn, not_1_out, not_2_out, not_3_out;

  not not_1 (not_1_out, inputalabel);
  not not_2 (not_2_out, inputb);
  not not_3 (not_3_out, in_4);
  and and_1 (and_1_out, not_3_out, in_4);
  and and_2 (and_2_out, not_1_out, inputb);
  or or_1 (output1, and_2_out, and_3_out);
  and and_3 (and_3_out, inputalabel, not_2_out);
  D_Flip_Flop d_ff_1 (.D(d_ff_1_qn), .clk(and_1_out), .Q(out_7), .Qn(d_ff_1_qn), .preset(in_3), .reset(in_5));
endmodule
