// Logisim project XNOR_up.circ as structural Verilog: 1 circuit, main circuit main
module main (
  input  in_1,
  input  in_2,
  output out_3
);

  wire transistor_1_out;

  Transistor transistor_1 (.in(1'b1), .out(transistor_1_out), .gate(in_1));
  Transistor #(.\type ("n")) transistor_2 (.in(1'b0), .out(transistor_1_out), .gate(in_1));
  Transistor transistor_3 (.in(transistor_1_out), .out(out_3), .gate(in_2));
  Transistor #(.\type ("n")) transistor_4 (.in(in_1), .out(out_3), .gate(in_2));
  // Transmission_Gate transmission_1: pin names not known; wires that end beside it: in_2, in_1, transistor_1_out, out_3
endmodule
