// Logisim project XNOR_t.circ as structural Verilog: 2 circuits, main circuit main
module main (
  input  inputalabel,
  input  inputb,
  input  in_3,
  input  in_4,
  output output1,
  output out_6
);

  wire and1_out, and_1_out, and_2_out, and_3_out, not_1_out, not_2_out, not_3_out, not_4_out, or_2_out;

  not not_1 (not_1_out, inputb);
  not not_2 (not_2_out, inputalabel);
  not not_3 (not_3_out, in_4);
  not not_4 (not_4_out, in_3);
  and and1 (and1_out, inputalabel, not_1_out);
  and and_1 (and_1_out, not_2_out, inputb);
  and and_2 (and_2_out, in_3, not_3_out);
  and and_3 (and_3_out, not_4_out, in_4);
  or or_1 (output1, and1_out, and_1_out);
  or or_2 (or_2_out, and_2_out, and_3_out);
  not not_5 (out_6, or_2_out);

  // Notes on the sheet:
  //   XOR
  //   XNOR
endmodule

module XOR1 (
  input  inputalabel,
  input  inputb,
  input  in_3,
  input  in_4,
  input  in_5,
  output output1,
  output out_7
);

  wire and_1_out, and_2_out, and_3_out, d_ff_1_qn, not_1_out, not_2_out, not_3_out;

  not not_1 (not_1_out, inputalabel);
  not not_2 (not_2_out, inputb);
  not not_3 (not_3_out, in_4);
  and and_1 (and_1_out, not_3_out, in_4);
  and and_2 (and_2_out, not_1_out, inputb);
  or or_1 (output1, and_2_out, and_3_out);
  and and_3 (and_3_out, inputalabel, not_2_out);
  D_Flip_Flop d_ff_1 (.D(d_ff_1_qn), .clk(and_1_out), .Q(out_7), .Qn(d_ff_1_qn), .preset(in_3), .reset(in_5));
endmodule
