// Logisim project XOR_up.circ as structural Verilog: 1 circuit, main circuit main
module main (
  input  in_1,
  input  in_2,
  output out_3
);

  wire transistor_1_out, transmission_1_p3;

  Transistor transistor_1 (.in(1'b1), .out(transistor_1_out), .gate(in_1));
  Transistor #(.\type ("n")) transistor_2 (.in(1'b0), .out(transistor_1_out), .gate(in_1));
  // Transmission_Gate transmission_1: pin names not known; wires that end beside it: in_1, in_2, transmission_1_p3, out_3
  // Transmission_Gate transmission_2: pin names not known; wires that end beside it: out_3, in_2, transmission_1_p3, transistor_1_out
  Transistor transistor_3 (.in(1'b1), .out(transmission_1_p3), .gate(in_2));
  Transistor #(.\type ("n")) transistor_4 (.in(1'b0), .out(transmission_1_p3), .gate(in_2));
endmodule
