// Logisim project logisimproject.circ as structural Verilog: 21 circuits, main circuit main
module main (
  input  C,
  input  A0,
  input  A1,
  input  A2,
  input  B0,
  input  A3,
  input  B1,
  input  S0,
  input  B2,
  input  S1,
  input  B3,
  input  S2,
  input  S3,
  output Cout
);

  Adder #(.width(4)) adder_1 (.a({A3, A2, A1, A0}), .b({B3, B2, B1, B0}), .out({S3, S2, S1, S0}), .cin(C), .cout(Cout));
endmodule

module decoder24 (
  input  A0,
  input  A1,
  output Y0,
  output Y1,
  output Y2,
  output Y3
);

  wire not_1_out, not_2_out;

  not not_1 (not_1_out, A0);
  not not_2 (not_2_out, A1);
  and and_1 (Y0, not_2_out, not_1_out);
  and and_2 (Y1, A0, not_2_out);
  and and_3 (Y2, not_1_out, A1);
  and and_4 (Y3, A0, A1);

  // Notes on the sheet:
  //   2-4译码器
endmodule

module decoder38 (
  input  A0,
  input  A1,
  input  A2,
  output Y0,
  output Y1,
  output Y2,
  output Y3,
  output Y4,
  output Y5,
  output Y6,
  output Y7
);

  wire decoder24_1_y0, decoder24_1_y1, decoder24_1_y2, decoder24_1_y3, not_1_out;

  not not_1 (not_1_out, A2);
  decoder24 decoder24_1 (
    .A0(A0), .A1(A1), .Y0(decoder24_1_y0), .Y1(decoder24_1_y1), .Y2(decoder24_1_y2), .Y3(decoder24_1_y3));
  and and_1 (Y0, decoder24_1_y0, not_1_out);
  and and_2 (Y1, decoder24_1_y1, not_1_out);
  and and_3 (Y2, decoder24_1_y2, not_1_out);
  and and_4 (Y3, decoder24_1_y3, not_1_out);
  and and_5 (Y4, decoder24_1_y0, A2);
  and and_6 (Y5, decoder24_1_y1, A2);
  and and_7 (Y6, decoder24_1_y2, A2);
  and and_8 (Y7, decoder24_1_y3, A2);
endmodule

module segment7display (
  input  A0,
  input  A1,
  input  A2,
  input  A3,
  output Y0,
  output Y1,
  output Y2,
  output Y3,
  output Y7,
  output Y6,
  output Y5,
  output Y4
);

  wire and_1_out, and_2_out, and_3_out, and_4_out, and_5_out, and_6_out, and_7_out, and_8_out, and_9_out,
       and_10_out, and_11_out, and_12_out, decoder38_1_y0, decoder38_1_y1, decoder38_1_y2, decoder38_1_y3,
       decoder38_1_y4, decoder38_1_y5, decoder38_1_y6, decoder38_1_y7, not_1_out;

  not not_1 (not_1_out, A3);
  decoder38 decoder38_1 (
    .A0(A0), .A1(A1), .A2(A2), .Y0(decoder38_1_y0), .Y1(decoder38_1_y1), .Y2(decoder38_1_y2),
    .Y3(decoder38_1_y3), .Y4(decoder38_1_y4), .Y5(decoder38_1_y5), .Y6(decoder38_1_y6), .Y7(decoder38_1_y7));
  and and_1 (and_1_out, decoder38_1_y0, not_1_out);
  and and_2 (and_2_out, decoder38_1_y1, not_1_out);
  and and_3 (and_3_out, decoder38_1_y2, not_1_out);
  and and_4 (and_4_out, decoder38_1_y3, not_1_out);
  and and_5 (and_5_out, decoder38_1_y4, not_1_out);
  and and_6 (and_6_out, decoder38_1_y5, not_1_out);
  and and_7 (and_7_out, decoder38_1_y6, not_1_out);
  and and_8 (and_8_out, decoder38_1_y7, not_1_out);
  and and_9 (and_9_out, decoder38_1_y0, A3);
  and and_10 (and_10_out, decoder38_1_y1, A3);
  and and_11 (and_11_out, A3, A2);
  and and_12 (and_12_out, A3, A1);
  or or_1 (Y7, and_11_out, and_12_out);
  or or_2 (Y3, and_10_out, and_9_out, and_8_out, and_5_out, and_4_out, and_3_out, and_2_out, and_1_out);
  or or_3 (Y0, and_10_out, and_9_out, and_7_out, and_6_out, and_5_out, and_4_out, and_3_out);
  or or_4 (Y1, and_1_out, and_10_out, and_9_out, and_7_out, and_5_out, and_6_out);
  or or_5 (Y4, and_1_out, and_3_out, and_7_out, and_9_out);
  _7_Segment_Display u_7_segment_display_1 (.g(Y0), .f(Y1), .a(Y2), .b(Y3), .e(Y4), .d(Y5), .c(Y6), .dp(Y7));
  nor nor_1 (Y2, and_2_out, and_5_out, Y7);
  nor nor_2 (Y6, Y7, and_3_out);
  or or_6 (Y5, and_1_out, and_3_out, and_4_out, and_6_out, and_7_out, and_9_out, and_10_out);
endmodule

module segment7display16 (
  input  A0,
  input  A1,
  input  A2,
  input  A3,
  output Y0,
  output Y1,
  output Y2,
  output Y3,
  output Y7,
  output Y6,
  output Y5,
  output Y4
);

  wire and_1_out, and_2_out, and_3_out, and_4_out, and_5_out, and_6_out, and_7_out, and_8_out, and_9_out,
       and_10_out, and_11_out, and_12_out, and_13_out, and_14_out, and_15_out, and_16_out, decoder38_1_y0,
       decoder38_1_y1, decoder38_1_y2, decoder38_1_y3, decoder38_1_y4, decoder38_1_y5, decoder38_1_y6,
       decoder38_1_y7, not_1_out;

  not not_1 (not_1_out, A3);
  decoder38 decoder38_1 (
    .A0(A0), .A1(A1), .A2(A2), .Y0(decoder38_1_y0), .Y1(decoder38_1_y1), .Y2(decoder38_1_y2),
    .Y3(decoder38_1_y3), .Y4(decoder38_1_y4), .Y5(decoder38_1_y5), .Y6(decoder38_1_y6), .Y7(decoder38_1_y7));
  and and_1 (and_1_out, decoder38_1_y0, not_1_out);
  and and_2 (and_2_out, decoder38_1_y1, not_1_out);
  and and_3 (and_3_out, decoder38_1_y2, not_1_out);
  and and_4 (and_4_out, decoder38_1_y3, not_1_out);
  and and_5 (and_5_out, decoder38_1_y4, not_1_out);
  and and_6 (and_6_out, decoder38_1_y5, not_1_out);
  and and_7 (and_7_out, decoder38_1_y6, not_1_out);
  and and_8 (and_8_out, decoder38_1_y7, not_1_out);
  and and_9 (and_9_out, decoder38_1_y0, A3);
  and and_10 (and_10_out, decoder38_1_y1, A3);
  and and_11 (and_11_out, A3, decoder38_1_y2);
  and and_12 (and_12_out, A3, decoder38_1_y3);
  and and_13 (and_13_out, A3, decoder38_1_y4);
  and and_14 (and_14_out, A3, decoder38_1_y5);
  and and_15 (and_15_out, A3, decoder38_1_y6);
  and and_16 (and_16_out, A3, decoder38_1_y7);
  nor nor_1 (Y3, and_6_out, and_7_out, and_13_out, and_15_out, and_16_out);
  nor nor_2 (Y0, and_1_out, and_2_out, and_8_out, and_14_out, and_13_out);
  nor nor_3 (Y1, and_2_out, and_3_out, and_4_out, and_8_out);
  nor nor_4 (Y4, and_2_out, and_4_out, and_5_out, and_6_out, and_8_out, and_10_out);
  _7_Segment_Display u_7_segment_display_1 (.g(Y0), .f(Y1), .a(Y2), .b(Y3), .e(Y4), .d(Y5), .c(Y6), .dp(Y7));
  nor nor_5 (Y2, and_2_out, and_5_out);
  nor nor_6 (Y6, and_13_out, and_15_out, and_16_out, and_3_out);
  nor nor_7 (Y5, and_8_out, and_2_out, and_5_out, and_10_out, and_11_out, and_16_out);
  or or_1 (Y7, and_11_out, and_12_out, and_13_out, and_14_out, and_15_out, and_16_out);
endmodule

module encoder16to4 (
  input  A0,
  input  A1,
  input  A2,
  input  A3,
  input  A4,
  input  A5,
  input  A6,
  input  A7,
  input  A8,
  input  A9,
  input  A10,
  input  A11,
  input  A12,
  input  A13,
  input  A14,
  input  A15,
  output Y0,
  output Y1,
  output Y2,
  output Y3
);

  or or_1 (Y0, A1, A3, A5, A7, A9, A11, A13, A15);
  or or_2 (Y1, A15, A14, A11, A10, A7, A6, A3, A2);
  or or_3 (Y3, A8, A9, A10, A11, A12, A13, A14, A15);
  or or_4 (Y2, A4, A5, A6, A7, A12, A13, A14, A15);
endmodule

module encoder16to4segment7 (
  input  A0,
  input  A1,
  input  A2,
  input  A3,
  input  A4,
  input  A5,
  input  A6,
  input  A7,
  input  A8,
  input  A9,
  input  A10,
  input  A11,
  input  A12,
  input  A13,
  input  A14,
  input  A15,
  output Y0,
  output Y1,
  output Y2,
  output Y3
);

  wire and_1_out, and_2_out, and_3_out, and_4_out, and_5_out, and_6_out, and_7_out, and_8_out, and_9_out,
       and_10_out, and_11_out, and_12_out, and_13_out, and_14_out, and_15_out, and_16_out, decoder38_1_y0,
       decoder38_1_y1, decoder38_1_y2, decoder38_1_y3, decoder38_1_y4, decoder38_1_y5, decoder38_1_y6,
       decoder38_1_y7, nor_1_out, nor_2_out, nor_3_out, nor_4_out, nor_5_out, nor_6_out, nor_7_out,
       not_1_out, or_5_out;

  or or_1 (Y0, A1, A3, A5, A7, A9, A11, A13, A15);
  or or_2 (Y1, A15, A14, A11, A10, A7, A6, A3, A2);
  or or_3 (Y3, A8, A9, A10, A11, A12, A13, A14, A15);
  or or_4 (Y2, A4, A5, A6, A7, A12, A13, A14, A15);
  not not_1 (not_1_out, Y3);
  decoder38 decoder38_1 (
    .A0(Y0), .A1(Y1), .A2(Y2), .Y0(decoder38_1_y0), .Y1(decoder38_1_y1), .Y2(decoder38_1_y2),
    .Y3(decoder38_1_y3), .Y4(decoder38_1_y4), .Y5(decoder38_1_y5), .Y6(decoder38_1_y6), .Y7(decoder38_1_y7));
  and and_1 (and_1_out, decoder38_1_y0, not_1_out);
  and and_2 (and_2_out, decoder38_1_y1, not_1_out);
  and and_3 (and_3_out, decoder38_1_y2, not_1_out);
  and and_4 (and_4_out, decoder38_1_y3, not_1_out);
  and and_5 (and_5_out, decoder38_1_y4, not_1_out);
  and and_6 (and_6_out, decoder38_1_y5, not_1_out);
  and and_7 (and_7_out, decoder38_1_y6, not_1_out);
  and and_8 (and_8_out, decoder38_1_y7, not_1_out);
  and and_9 (and_9_out, decoder38_1_y0, Y3);
  and and_10 (and_10_out, decoder38_1_y1, Y3);
  and and_11 (and_11_out, Y3, decoder38_1_y2);
  and and_12 (and_12_out, Y3, decoder38_1_y3);
  and and_13 (and_13_out, Y3, decoder38_1_y4);
  and and_14 (and_14_out, Y3, decoder38_1_y5);
  and and_15 (and_15_out, Y3, decoder38_1_y6);
  and and_16 (and_16_out, Y3, decoder38_1_y7);
  nor nor_1 (nor_1_out, and_6_out, and_7_out, and_13_out, and_15_out, and_16_out);
  nor nor_2 (nor_2_out, and_2_out, and_4_out, and_5_out, and_6_out, and_8_out, and_10_out);
  nor nor_3 (nor_3_out, and_1_out, and_2_out, and_8_out, and_14_out, and_13_out);
  nor nor_4 (nor_4_out, and_2_out, and_3_out, and_4_out, and_8_out);
  _7_Segment_Display u_7_segment_display_1 (
    .g(nor_3_out), .f(nor_4_out), .a(nor_5_out), .b(nor_1_out), .e(nor_2_out), .d(nor_7_out), .c(nor_6_out),
    .dp(or_5_out));
  nor nor_5 (nor_5_out, and_2_out, and_5_out);
  nor nor_6 (nor_6_out, and_13_out, and_15_out, and_16_out, and_3_out);
  nor nor_7 (nor_7_out, and_8_out, and_2_out, and_5_out, and_10_out, and_11_out, and_16_out);
  or or_5 (or_5_out, and_11_out, and_12_out, and_13_out, and_14_out, and_15_out, and_16_out);
endmodule

module priorityencoder4to2 (
  input  A0,
  input  A1,
  input  A2,
  input  A3,
  output Y1,
  output Y0,
  output V
);

  wire and_1_out, not_1_out;

  not not_1 (not_1_out, A2);
  and and_1 (and_1_out, A1, not_1_out);
  or or_1 (Y1, A2, A3);
  or or_2 (Y0, and_1_out, A3);
  or or_3 (V, A0, A1, A3, A2);
endmodule

module priorityencoder16to4 (
  input  A0,
  input  A1,
  input  A2,
  input  A3,
  input  A4,
  input  A5,
  input  A6,
  input  A7,
  input  A8,
  input  A9,
  input  A10,
  input  A11,
  input  A12,
  input  A13,
  input  A14,
  input  A15,
  output Y0,
  output Y1,
  output Y2,
  output Y3,
  output V
);

  wire priorityencoder4to2_1_v, priorityencoder4to2_1_y0, priorityencoder4to2_1_y1, priorityencoder4to2_2_v,
       priorityencoder4to2_2_y0, priorityencoder4to2_2_y1, priorityencoder4to2_3_v, priorityencoder4to2_3_y0,
       priorityencoder4to2_3_y1, priorityencoder4to2_4_v, priorityencoder4to2_4_y0, priorityencoder4to2_4_y1;

  priorityencoder4to2 priorityencoder4to2_1 (
    .A0(A0), .A1(A1), .A2(A2), .A3(A3), .Y1(priorityencoder4to2_1_y1), .Y0(priorityencoder4to2_1_y0),
    .V(priorityencoder4to2_1_v));
  priorityencoder4to2 priorityencoder4to2_2 (
    .A0(A4), .A1(A5), .A2(A6), .A3(A7), .Y1(priorityencoder4to2_2_y1), .Y0(priorityencoder4to2_2_y0),
    .V(priorityencoder4to2_2_v));
  priorityencoder4to2 priorityencoder4to2_3 (
    .A0(A8), .A1(A9), .A2(A10), .A3(A11), .Y1(priorityencoder4to2_3_y1), .Y0(priorityencoder4to2_3_y0),
    .V(priorityencoder4to2_3_v));
  priorityencoder4to2 priorityencoder4to2_4 (
    .A0(A12), .A1(A13), .A2(A14), .A3(A15), .Y1(priorityencoder4to2_4_y1), .Y0(priorityencoder4to2_4_y0),
    .V(priorityencoder4to2_4_v));
  Multiplexer #(.select(2)) multiplexer_1 (
    .in0(priorityencoder4to2_1_y0), .in1(priorityencoder4to2_2_y0), .in2(priorityencoder4to2_3_y0),
    .in3(priorityencoder4to2_4_y0), .out(Y0), .sel({Y3, Y2}));
  Multiplexer #(.select(2)) multiplexer_2 (
    .in0(priorityencoder4to2_1_y1), .in1(priorityencoder4to2_2_y1), .in2(priorityencoder4to2_3_y1),
    .in3(priorityencoder4to2_4_y1), .out(Y1), .sel({Y3, Y2}));
  priorityencoder4to2 priorityencoder4to2_5 (
    .A0(priorityencoder4to2_1_v), .A1(priorityencoder4to2_2_v), .A2(priorityencoder4to2_3_v),
    .A3(priorityencoder4to2_4_v), .Y1(Y3), .Y0(Y2), .V(V));
  segment7display16 segment7display16_1 (.Y0(Y0), .Y1(Y1), .Y2(Y2), .Y3(Y3));  // open: A3, A0, A1, A2, Y4, Y5, Y6, Y7
endmodule

module NumberOfleadingZeros (
  input  [15:0] in_1,
  output [3:0] out_2
);

  wire [3:0] priorityencoder16to4_1_y0;

  priorityencoder16to4 priorityencoder16to4_1 (
    .A0(in_1[0]), .A1(in_1[1]), .A2(in_1[2]), .A3(in_1[3]), .A4(in_1[4]), .A5(in_1[5]), .A6(in_1[6]),
    .A7(in_1[7]), .A8(in_1[8]), .A9(in_1[9]), .A10(in_1[10]), .A11(in_1[11]), .A12(in_1[12]), .A13(in_1[13]),
    .A14(in_1[14]), .A15(in_1[15]), .Y0(priorityencoder16to4_1_y0[0]), .Y1(priorityencoder16to4_1_y0[1]),
    .Y2(priorityencoder16to4_1_y0[2]), .Y3(priorityencoder16to4_1_y0[3]));  // open: V
  assign out_2 = ~priorityencoder16to4_1_y0;  // NOT_Gate not_1, 4 bits wide
endmodule

module NumberOfleadingOnes (
  input  [15:0] in_1,
  output [3:0] out_2
);

  wire [3:0] priorityencoder16to4_1_y0;
  wire [15:0] not_1_out;

  assign not_1_out = ~in_1;  // NOT_Gate not_1, 16 bits wide
  priorityencoder16to4 priorityencoder16to4_1 (
    .A0(not_1_out[0]), .A1(not_1_out[1]), .A2(not_1_out[2]), .A3(not_1_out[3]), .A4(not_1_out[4]),
    .A5(not_1_out[5]), .A6(not_1_out[6]), .A7(not_1_out[7]), .A8(not_1_out[8]), .A9(not_1_out[9]),
    .A10(not_1_out[10]), .A11(not_1_out[11]), .A12(not_1_out[12]), .A13(not_1_out[13]), .A14(not_1_out[14]),
    .A15(not_1_out[15]), .Y0(priorityencoder16to4_1_y0[0]), .Y1(priorityencoder16to4_1_y0[1]),
    .Y2(priorityencoder16to4_1_y0[2]), .Y3(priorityencoder16to4_1_y0[3]));  // open: V
  assign out_2 = ~priorityencoder16to4_1_y0;  // NOT_Gate not_2, 4 bits wide
endmodule

module Multiplexer2to1 (
  input  D0,
  input  S,
  input  D1,
  output Y
);

  wire and_1_out, and_2_out, not_1_out;

  not not_1 (not_1_out, S);
  and and_1 (and_1_out, D0, not_1_out);
  and and_2 (and_2_out, S, D1);
  or or_1 (Y, and_1_out, and_2_out);
endmodule

module Multiplexer4to1 (
  input  S0,
  input  S1,
  input  D0,
  input  D1,
  input  D2,
  input  D3,
  output Y
);

  wire and_1_out, and_2_out, and_3_out, and_4_out, not_1_out, not_2_out;

  not not_1 (not_1_out, S0);
  not not_2 (not_2_out, S1);
  and and_1 (and_1_out, not_1_out, D0, not_2_out);
  and and_2 (and_2_out, not_2_out, D1, S0);
  and and_3 (and_3_out, S1, D2, not_1_out);
  and and_4 (and_4_out, S0, D3, S1);
  or or_1 (Y, and_1_out, and_2_out, and_3_out, and_4_out);
endmodule

module BIT3Multiplexer4to1 (
  input  [1:0] in_1,
  input  [2:0] in_2,
  input  [2:0] in_3,
  input  [2:0] in_4,
  input  [2:0] in_5,
  output [2:0] out_6
);

  Multiplexer4to1 multiplexer4to1_1 (
    .S0(in_1[0]), .S1(in_1[1]), .D0(in_2[0]), .D1(in_3[0]), .D2(in_4[0]), .D3(in_5[0]), .Y(out_6[0]));
  Multiplexer4to1 multiplexer4to1_2 (
    .S0(in_1[0]), .S1(in_1[1]), .D0(in_2[1]), .D1(in_3[1]), .D2(in_4[1]), .D3(in_5[1]), .Y(out_6[1]));
  Multiplexer4to1 multiplexer4to1_3 (
    .S0(in_1[0]), .S1(in_1[1]), .D0(in_2[2]), .D1(in_3[2]), .D2(in_4[2]), .D3(in_5[2]), .Y(out_6[2]));
endmodule

module TEST3512 (
);

  wire dipswitch_1_sw1, dipswitch_1_sw2, dipswitch_1_sw3, dipswitch_1_sw4, dipswitch_1_sw5;
  wire [7:0] multiplexer_1_out, segment7display16_1_y0, segment7display_1_y0;

  DipSwitch #(.number(5)) dipswitch_1 (
    .sw1(dipswitch_1_sw1), .sw2(dipswitch_1_sw2), .sw3(dipswitch_1_sw3), .sw4(dipswitch_1_sw4),
    .sw5(dipswitch_1_sw5));
  segment7display segment7display_1 (
    .A3(dipswitch_1_sw4), .A0(dipswitch_1_sw1), .A1(dipswitch_1_sw2), .A2(dipswitch_1_sw3),
    .Y4(segment7display_1_y0[7]), .Y1(segment7display_1_y0[1]), .Y5(segment7display_1_y0[6]),
    .Y2(segment7display_1_y0[2]), .Y3(segment7display_1_y0[3]), .Y7(segment7display_1_y0[4]),
    .Y0(segment7display_1_y0[0]), .Y6(segment7display_1_y0[5]));
  segment7display16 segment7display16_1 (
    .A3(dipswitch_1_sw4), .A0(dipswitch_1_sw1), .A1(dipswitch_1_sw2), .A2(dipswitch_1_sw3),
    .Y4(segment7display16_1_y0[7]), .Y0(segment7display16_1_y0[0]), .Y5(segment7display16_1_y0[6]),
    .Y1(segment7display16_1_y0[1]), .Y2(segment7display16_1_y0[2]), .Y6(segment7display16_1_y0[5]),
    .Y3(segment7display16_1_y0[3]), .Y7(segment7display16_1_y0[4]));
  Multiplexer #(.width(8)) multiplexer_1 (
    .in0(segment7display_1_y0), .in1(segment7display16_1_y0), .out(multiplexer_1_out), .sel(dipswitch_1_sw5));
  _7_Segment_Display u_7_segment_display_1 (
    .g(multiplexer_1_out[0]), .f(multiplexer_1_out[1]), .a(multiplexer_1_out[2]), .b(multiplexer_1_out[3]),
    .e(multiplexer_1_out[7]), .d(multiplexer_1_out[6]), .c(multiplexer_1_out[5]), .dp(multiplexer_1_out[4]));
endmodule

module comparator4 (
  input  A0,
  input  B0,
  input  A1,
  input  B1,
  input  A2,
  input  B2,
  input  A3,
  input  B3,
  output Y
);

  wire xnor_1_out, xnor_2_out, xnor_3_out, xnor_4_out;

  xnor xnor_1 (xnor_1_out, A0, B0);
  xnor xnor_2 (xnor_2_out, A1, B1);
  xnor xnor_3 (xnor_3_out, A2, B2);
  xnor xnor_4 (xnor_4_out, A3, B3);
  and and_1 (Y, xnor_1_out, xnor_2_out, xnor_3_out, xnor_4_out);
endmodule

module TEST3513 (
);

  wire comparator4_1_y, dipswitch_1_p1, dipswitch_1_p2, dipswitch_1_p3, dipswitch_1_p4, dipswitch_2_p1,
       dipswitch_2_p2, dipswitch_2_p3, dipswitch_2_p4;

  // DipSwitch #(.number(4)) dipswitch_1: pin names not known; wires that end beside it: dipswitch_1_p1, dipswitch_1_p2, dipswitch_1_p3, dipswitch_1_p4
  // DipSwitch #(.number(4)) dipswitch_2: pin names not known; wires that end beside it: dipswitch_2_p1, dipswitch_2_p2, dipswitch_2_p3, dipswitch_2_p4
  LED led_1 (.in(comparator4_1_y));
  comparator4 comparator4_1 (
    .A0(dipswitch_1_p1), .B0(dipswitch_2_p1), .A1(dipswitch_1_p2), .B1(dipswitch_2_p2), .A2(dipswitch_1_p3),
    .B2(dipswitch_2_p3), .A3(dipswitch_1_p4), .B3(dipswitch_2_p4), .Y(comparator4_1_y));
endmodule

module FullAdder1biT (
  input  A,
  input  B,
  input  C,
  output S,
  output Cout
);

  wire and_1_out, and_2_out, and_3_out, and_4_out, and_5_out, and_6_out, and_7_out, not_1_out, not_2_out,
       not_3_out;

  not not_1 (not_1_out, A);
  not not_2 (not_2_out, B);
  not not_3 (not_3_out, C);
  and and_1 (and_1_out, not_1_out, not_2_out, C);
  and and_2 (and_2_out, not_1_out, B, not_3_out);
  and and_3 (and_3_out, A, not_2_out, not_3_out);
  and and_4 (and_4_out, A, B, C);
  and and_5 (and_5_out, B, C);
  and and_6 (and_6_out, A, C);
  and and_7 (and_7_out, A, B);
  or or_1 (S, and_1_out, and_2_out, and_3_out, and_4_out);
  or or_2 (Cout, and_5_out, and_6_out, and_7_out);
endmodule

module HalfAdder1bit (
  input  A,
  input  B,
  output S,
  output C
);

  xor xor_1 (S, A, B);
  and and_1 (C, A, B);
endmodule

module FulAdder1bit (
  input  in_1,
  input  in_2,
  input  in_3,
  output S,
  output Cout
);

  wire halfadder1bit_1_c, halfadder1bit_1_s, halfadder1bit_2_c;

  HalfAdder1bit halfadder1bit_1 (.A(in_2), .B(in_3), .S(halfadder1bit_1_s), .C(halfadder1bit_1_c));
  HalfAdder1bit halfadder1bit_2 (.A(in_1), .B(halfadder1bit_1_s), .S(S), .C(halfadder1bit_2_c));
  HalfAdder1bit halfadder1bit_3 (.A(halfadder1bit_2_c), .B(halfadder1bit_1_c), .S(Cout));  // open: C
endmodule

module Adder4bit (
  input  C,
  input  A0,
  input  B0,
  input  A1,
  input  B1,
  input  A2,
  input  B2,
  input  A3,
  input  B3,
  output S0,
  output S1,
  output S2,
  output S3,
  output Cout
);

  wire and_1_out, and_2_out, and_3_out, and_4_out, and_5_out, and_6_out, and_7_out, and_8_out, or_1_out,
       or_2_out, or_3_out, xor_1_out, xor_2_out, xor_3_out, xor_4_out;

  xor xor_1 (xor_1_out, A0, B0);
  and and_1 (and_1_out, A0, B0);
  xor xor_2 (xor_2_out, A1, B1);
  and and_2 (and_2_out, A1, B1);
  xor xor_3 (xor_3_out, A2, B2);
  and and_3 (and_3_out, A2, B2);
  xor xor_4 (xor_4_out, A3, B3);
  and and_4 (and_4_out, A3, B3);
  or or_1 (or_1_out, and_5_out, and_1_out);
  xor xor_5 (S0, C, xor_1_out);
  and and_5 (and_5_out, C, xor_1_out);
  xor xor_6 (S1, or_1_out, xor_2_out);
  and and_6 (and_6_out, or_1_out, xor_2_out);
  or or_2 (or_2_out, and_6_out, and_2_out);
  xor xor_7 (S2, or_2_out, xor_3_out);
  and and_7 (and_7_out, or_2_out, xor_3_out);
  or or_3 (or_3_out, and_7_out, and_3_out);
  xor xor_8 (S3, or_3_out, xor_4_out);
  and and_8 (and_8_out, or_3_out, xor_4_out);
  or or_4 (Cout, and_8_out, and_4_out);
  segment7display16 segment7display16_1 (.A3(S3), .A0(S0), .A1(S1), .A2(S2));  // open: Y4, Y0, Y5, Y1, Y2, Y6, Y3, Y7
  LED led_1 (.in(Cout));
endmodule
